// Logisim project cpu.circ as structural Verilog: 1 circuit, main circuit main
module main (
  input  [31:0] RS_READ_VALUE,
  input  [31:0] RT_READ_VALUE,
  input  [31:0] INSTRUCTION,
  input  CLOCK,
  input  RESET,
  output [31:0] t0,
  output [31:0] t1,
  output [31:0] t2,
  output [31:0] t3,
  output [4:0] RS,
  output [4:0] RT,
  output [4:0] Write_Register,
  output [31:0] RD_WRITE_VALUE,
  output RD_WRITE_ENABLE,
  output [23:0] FETCH_ADDRESS
);

  wire [4:0] rd, rs_t, rt_t, shamt;
  wire [5:0] funct, op;
  wire [15:0] immediate;
  wire [25:0] addresss;
  wire [31:0] and_1_out, and_2_out, and_3_out, and_4_out, and_5_out, and_6_out, and_7_out, and_8_out,
       shifter_1_out, shifter_2_out, shifter_3_out, shifter_4_out, shifter_5_out, shifter_6_out,
       shifter_7_out, shifter_8_out;

  // regfile_main RegFile: pin names not known
  // mem_main MEM: pin names not known
  // alu_main ALU: pin names not known
  assign and_1_out = INSTRUCTION & 32'hfc000000;  // AND_Gate and_1, 32 bits wide
  assign and_2_out = INSTRUCTION & 32'h3e00000;  // AND_Gate and_2, 32 bits wide
  assign and_3_out = INSTRUCTION & 32'h1f0000;  // AND_Gate and_3, 32 bits wide
  assign and_4_out = INSTRUCTION & 32'hf800;  // AND_Gate and_4, 32 bits wide
  assign and_5_out = INSTRUCTION & 32'h7c00;  // AND_Gate and_5, 32 bits wide
  assign and_6_out = INSTRUCTION & 32'h3f;  // AND_Gate and_6, 32 bits wide
  assign and_7_out = INSTRUCTION & 32'hffff;  // AND_Gate and_7, 32 bits wide
  assign and_8_out = INSTRUCTION & 32'h3ffffff;  // AND_Gate and_8, 32 bits wide
  Shifter #(.width(32), .shift("lr")) shifter_1 (.in(and_1_out), .\dist (5'b11010), .out(shifter_1_out));
  Shifter #(.width(32), .shift("lr")) shifter_2 (.in(and_2_out), .\dist (5'b10101), .out(shifter_2_out));
  Shifter #(.width(32), .shift("lr")) shifter_3 (.in(and_3_out), .\dist (5'b10000), .out(shifter_3_out));
  Shifter #(.width(32), .shift("lr")) shifter_4 (.in(and_4_out), .\dist (5'b01011), .out(shifter_4_out));
  Shifter #(.width(32), .shift("lr")) shifter_5 (.in(and_5_out), .\dist (5'b00110), .out(shifter_5_out));
  Shifter #(.width(32), .shift("lr")) shifter_6 (.in(and_6_out), .\dist ({5{1'b0}}), .out(shifter_6_out));
  Shifter #(.width(32), .shift("lr")) shifter_7 (.in(and_7_out), .\dist ({5{1'b0}}), .out(shifter_7_out));
  Shifter #(.width(32), .shift("lr")) shifter_8 (.in(and_8_out), .\dist ({5{1'b0}}), .out(shifter_8_out));
  Bit_Extender #(.in_width(32), .out_width(6)) bit_extender_1 (.in(shifter_1_out), .out(op));
  Bit_Extender #(.in_width(32), .out_width(5)) bit_extender_2 (.in(shifter_2_out), .out(rs_t));
  Bit_Extender #(.in_width(32), .out_width(5)) bit_extender_3 (.in(shifter_3_out), .out(rt_t));
  Bit_Extender #(.in_width(32), .out_width(5)) bit_extender_4 (.in(shifter_4_out), .out(rd));
  Bit_Extender #(.in_width(32), .out_width(5)) bit_extender_5 (.in(shifter_5_out), .out(shamt));
  Bit_Extender #(.in_width(32), .out_width(6)) bit_extender_6 (.in(shifter_6_out), .out(funct));
  Bit_Extender #(.in_width(32)) bit_extender_7 (.in(shifter_7_out), .out(immediate));
  Bit_Extender #(.in_width(32), .out_width(26)) bit_extender_8 (.in(shifter_8_out), .out(addresss));
  // Probe on op
  // Probe on rs_t
  // Probe on rt_t
  // Probe on rd
  // Probe on shamt
  // Probe on funct
  // Probe on immediate
  // Probe on addresss
  Adder #(.width(2)) adder_1 ();  // open: a, b, out, cin, cout

  // Other names for the same wires on the sheet: FETCH_ADDRES[23:0] = FETCH_ADDRESS;
  //   RD_WRITE_VALU[31:0] = RD_WRITE_VALUE; RT_READ_VALU[31:0] = RT_READ_VALUE

  // Notes on the sheet:
  //   These are outputs/inputs from run.circ
  //   Decode
endmodule
